# Fritzing sketch micro-mega-schematic (saved by Fritzing 0.9.3b)
breadboards: 2

parts:
  Atmega1 = ATmega1284
  U1 = LCD-16X2 [package=lcd-16x2]
  R1 = TRIMPOT [package=trim_pot_pth]
  JP1 = M16 [package=1x16_machine-pin-header_lock.004]

nets:
  N1: Atmega1.PC0, U1.DB0, JP1.7
  N2: Atmega1.PC1, U1.DB1, JP1.8
  N3: Atmega1.PC2, U1.DB2, JP1.9
  N4: Atmega1.PC3, U1.DB3, JP1.10
  N5: Atmega1.PC4, U1.DB4, JP1.11
  N6: Atmega1.PC5, U1.DB5, JP1.12
  N7: Atmega1.PC6, U1.DB6, JP1.13
  N8: Atmega1.PC7, U1.DB7, JP1.14
  N9: Atmega1.AVCC, U1.VDD, U1.A, R1.CW, JP1.2, JP1.15
  N10: Atmega1.GND#30, U1.VSS, U1.R_W, U1.K, R1.CCW, JP1.1, JP1.5, JP1.16
  N11: Atmega1.PA1, U1.E, JP1.6
  N12: Atmega1.PA0, U1.RS, JP1.4
  N13: U1.VO, R1.WIPER, JP1.3

notes:
  To Power Supply
  PS/2 Data Line
  PS/2 Clock

custom parts:
  ATmega1284: AVR 8-bit microcontroller.
